# Fritzing sketch ESP8266BreadboardCircuit (saved by Fritzing 0.7.12b)
breadboards: 1

parts:
  Part1 = SparkFun ESP8266 Thing
  Part2 = FTDI Basic Programmer
  LED1 = LED - 5mm [color="Red (633nm)" package="5 mm [THT]"]
  S1 = Pushbutton [package="[THT]"]
  R1 = Resistor [tolerance=±5% resistance=330 package=THT]
  R2 = Resistor [tolerance=±5% resistance=10k package=THT]

nets:
  N1: Part1.RESET, Part2.DTR
  N2: Part1.U0TXO, Part2.RXI
  N3: Part1.U0RXI, Part2.TXO
  N4: Part1.USBVCC, Part2.POWER
  N5: Part1.9, Part2.CTS
  GND: Part1.GND, Part2.GND, S1.Pin_3, S1.Pin_4, R1.Pin_0
  N6: Part1.VIN, R2.Pin_1
  N7: Part1.GPIO4, LED1.anode
  N8: Part1.GPIO12, S1.Pin_1, S1.Pin_2, R2.Pin_0
  N9: LED1.cathode, R1.Pin_1
